# Fritzing sketch physicalDesign (saved by Fritzing 1.0.1rc)
breadboards: 1

parts:
  Mod1 = Raspberry Pi 4B
  HC-SR04_Sensor_1 = HC-SR04 Ultrasonic Distance Sensor
  LED1 = smd LED [color="Red (633nm)" package="0603 [SMD]"]
  R1 = Resistor [tolerance=±5% resistance=220 package="2010 [SMD]"]

nets:
  5V: Mod1.5V, HC-SR04_Sensor_1.VCC
  GND: Mod1.GND, HC-SR04_Sensor_1.GND, R1.Pin_0
  N1: Mod1.GPIO17, HC-SR04_Sensor_1.TRIG
  N2: Mod1.GPIO27, HC-SR04_Sensor_1.ECHO
  N3: Mod1.GPIO25, LED1.anode
  N4: LED1.cathode, R1.Pin_1
